# Fritzing sketch Buzzer2 (saved by Fritzing 0.9.10b)
circuit board: 3.43202cm x 1.90086cm
breadboards: 1

parts:
  Atmega328P-AU = ATmega328 [package=tqfp]
  MS5611 = MPL3115A2 [package=lga8]
  Q1 = PNP-Transistor [package="SOT-23 [SMD]"]
  KSSGJ44B20 = Piezo Speaker
  U2 = PIC-ICSP-Mini [package=pic-icsp-mini]

nets:
  GND: Atmega328P-AU.GND, Atmega328P-AU.AGND, MS5611.GND, MS5611.SCB, MS5611.INT1, KSSGJ44B20.pin1, KSSGJ44B20.pin_4, U2.GND
  VCC: Atmega328P-AU.VCC, Atmega328P-AU.AVCC, MS5611.VDD, MS5611.PS, Q1.2, U2.VCC
  N1: Atmega328P-AU.PB1(OC1A), Q1.0
  N2: Atmega328P-AU.PC4(ADC4_SDA), MS5611.SDA
  N3: Atmega328P-AU.PC5(ADC5_SCL), MS5611.SCL
  N4: Atmega328P-AU.PC6(_RESET), U2.RESET
  N5: Atmega328P-AU.PD0(RXD), U2.RX
  N6: Atmega328P-AU.PD1(TXD), U2.TX
  N7: Q1.1, KSSGJ44B20.pin2, KSSGJ44B20.pin_3

custom parts:
  MPL3115A2: Altimeter/Pressure Sensor, I2C, 1.95V-3.6V supply, 50 to 110kPa
  Piezo Speaker: Piezo
  PIC-ICSP-Mini: PIC-ICSP-Mini Miniature 5-pin connection for temporary programming of PICs. Use this device in your design to save space. Program the PIC with this adapter Spark Fun Electronics SKU : BOB-00194
